// Logisim project Assignment_12_Circuits.circ as structural Verilog
module Half_Adder (
  input  Input_X,
  input  Input_Y,
  output Sum,
  output Carry
);

  xor xor_1 (Sum, Input_X, Input_Y);
  and and_1 (Carry, Input_X, Input_Y);
endmodule

module Full_Adder (
  input  Input_X,
  input  Input_Y,
  input  Cin,
  output Sum,
  output out_5
);

  wire half_adder_1_carry, half_adder_1_sum, half_adder_2_carry;

  Half_Adder half_adder_1 (.Input_X(Input_X), .Input_Y(Input_Y), .Sum(half_adder_1_sum), .Carry(half_adder_1_carry));
  Half_Adder half_adder_2 (.Input_X(half_adder_1_sum), .Input_Y(Cin), .Sum(Sum), .Carry(half_adder_2_carry));
  or or_1 (out_5, half_adder_2_carry, half_adder_1_carry);
endmodule

module Problem1_8BitAdder (
  input  Cin,
  input  X0,
  input  Y0,
  input  X1,
  input  Y1,
  input  X2,
  input  Y2,
  input  X3,
  input  Y3,
  input  X4,
  input  Y4,
  input  X5,
  input  Y5,
  input  X6,
  input  Y6,
  input  X7,
  input  Y7,
  output S0,
  output S1,
  output S2,
  output S3,
  output S4,
  output S5,
  output S6,
  output S7
);

  wire full_adder_1_out_5, full_adder_2_out_5, full_adder_3_out_5, full_adder_4_out_5, full_adder_5_out_5,
       full_adder_6_out_5, full_adder_7_out_5;

  Full_Adder full_adder_1 (.Input_X(Cin), .Input_Y(X0), .Cin(Y0), .Sum(S0), .out_5(full_adder_1_out_5));
  Full_Adder full_adder_2 (.Input_X(full_adder_1_out_5), .Input_Y(X1), .Cin(Y1), .Sum(S1), .out_5(full_adder_2_out_5));
  Full_Adder full_adder_3 (.Input_X(full_adder_2_out_5), .Input_Y(X2), .Cin(Y2), .Sum(S2), .out_5(full_adder_3_out_5));
  Full_Adder full_adder_4 (.Input_X(full_adder_3_out_5), .Input_Y(X3), .Cin(Y3), .Sum(S3), .out_5(full_adder_4_out_5));
  Full_Adder full_adder_5 (.Input_X(full_adder_4_out_5), .Input_Y(X4), .Cin(Y4), .Sum(S4), .out_5(full_adder_5_out_5));
  Full_Adder full_adder_6 (.Input_X(full_adder_5_out_5), .Input_Y(X5), .Cin(Y5), .Sum(S5), .out_5(full_adder_6_out_5));
  Full_Adder full_adder_7 (.Input_X(full_adder_6_out_5), .Input_Y(X6), .Cin(Y6), .Sum(S6), .out_5(full_adder_7_out_5));
  Full_Adder full_adder_8 (.Input_X(full_adder_7_out_5), .Input_Y(X7), .Cin(Y7), .Sum(S7));  // open: out_5

  // Notes on the sheet:
  //   8 Bit Adder Circuit using Full_Adder Circuits
endmodule

module Problem2_1Bit_Adder_Decoder (
  input  Input_A,
  input  Input_B,
  input  Cin,
  output Sum,
  output Carry
);

  wire decoder_1_out1, decoder_1_out2, decoder_1_out3, decoder_1_out4, decoder_1_out5, decoder_1_out6,
       decoder_1_out7;

  Decoder #(.select(3), .enable("false")) decoder_1 (
    .out1(decoder_1_out1), .out2(decoder_1_out2), .out3(decoder_1_out3), .out4(decoder_1_out4),
    .out5(decoder_1_out5), .out6(decoder_1_out6), .out7(decoder_1_out7), .sel({Cin, Input_B, Input_A}));  // open: out0
  or or_1 (Sum, decoder_1_out1, decoder_1_out2, decoder_1_out4, decoder_1_out7);
  or or_2 (Carry, decoder_1_out3, decoder_1_out5, decoder_1_out6, decoder_1_out7);

  // Notes on the sheet:
  //   1 bit adder using a decoder circuit
endmodule

module Problem2_4BitAdderDecoder (
  input  Cin,
  input  [3:0] Input_A,
  input  [3:0] Input_B,
  output [3:0] Sum,
  output Carry
);

  wire problem2_1bit_adder_decoder_1_carry, problem2_1bit_adder_decoder_2_carry,
       problem2_1bit_adder_decoder_3_carry;

  Problem2_1Bit_Adder_Decoder problem2_1bit_adder_decoder_1 (
    .Input_A(Cin), .Input_B(Input_A[0]), .Cin(Input_B[0]), .Sum(Sum[0]),
    .Carry(problem2_1bit_adder_decoder_1_carry));
  Problem2_1Bit_Adder_Decoder problem2_1bit_adder_decoder_2 (
    .Input_A(problem2_1bit_adder_decoder_1_carry), .Input_B(Input_A[1]), .Cin(Input_B[1]), .Sum(Sum[1]),
    .Carry(problem2_1bit_adder_decoder_2_carry));
  Problem2_1Bit_Adder_Decoder problem2_1bit_adder_decoder_3 (
    .Input_A(problem2_1bit_adder_decoder_2_carry), .Input_B(Input_A[2]), .Cin(Input_B[2]), .Sum(Sum[2]),
    .Carry(problem2_1bit_adder_decoder_3_carry));
  Problem2_1Bit_Adder_Decoder problem2_1bit_adder_decoder_4 (
    .Input_A(problem2_1bit_adder_decoder_3_carry), .Input_B(Input_A[3]), .Cin(Input_B[3]), .Sum(Sum[3]),
    .Carry(Carry));

  // Notes on the sheet:
  //   1 Bit Adder using decoder circuit modifyed to handle 4 bits and using Ripple-Carry Adder as template for circuit design 
endmodule

module Problem3_4x1Multiplexor (
  input  [7:0] _8,
  input  [7:0] _16,
  input  [7:0] _32,
  input  [7:0] _64,
  input  [1:0] Selection_Bit,
  output [7:0] out_6
);

  wire [7:0] multiplexer_1_out, multiplexer_2_out;

  Multiplexer #(.width(8), .disabled(0), .enable("false")) multiplexer_1 (
    .in0(_8), .in1(_16), .out(multiplexer_1_out), .sel(Selection_Bit[0]));
  Multiplexer #(.width(8), .disabled(0), .enable("false")) multiplexer_2 (
    .in0(_32), .in1(_64), .out(multiplexer_2_out), .sel(Selection_Bit[0]));
  Multiplexer #(.width(8), .disabled(0), .enable("false")) multiplexer_3 (
    .in0(multiplexer_1_out), .in1(multiplexer_2_out), .out(out_6), .sel(Selection_Bit[1]));

  // Notes on the sheet:
  //   Multiplexor which has a data width of 8 bits and 2 selection bits
endmodule

module Problem4_16x1_Multiplexor (
  input  [7:0] in_1,
  input  [7:0] in_2,
  input  [7:0] in_3,
  input  [7:0] in_4,
  input  [7:0] in_5,
  input  [7:0] in_6,
  input  [7:0] in_7,
  input  [7:0] in_8,
  input  [7:0] in_9,
  input  [7:0] in_10,
  input  [7:0] in_11,
  input  [7:0] in_12,
  input  [7:0] in_13,
  input  [7:0] in_14,
  input  [7:0] in_15,
  input  [7:0] in_16,
  input  [3:0] Selection_Bit,
  output [7:0] out_18
);

  wire [7:0] multiplexer_1_out, multiplexer_2_out, multiplexer_3_out, multiplexer_4_out;

  Multiplexer #(.select(2), .width(8), .disabled(0), .enable("false")) multiplexer_1 (
    .in0(in_1), .in1(in_2), .in2(in_3), .in3(in_4), .out(multiplexer_1_out), .sel(Selection_Bit[1:0]));
  Multiplexer #(.select(2), .width(8), .disabled(0), .enable("false")) multiplexer_2 (
    .in0(in_5), .in1(in_6), .in2(in_7), .in3(in_8), .out(multiplexer_2_out), .sel(Selection_Bit[1:0]));
  Multiplexer #(.select(2), .width(8), .disabled(0), .enable("false")) multiplexer_3 (
    .in0(in_9), .in1(in_10), .in2(in_11), .in3(in_12), .out(multiplexer_3_out), .sel(Selection_Bit[1:0]));
  Multiplexer #(.select(2), .width(8), .disabled(0), .enable("false")) multiplexer_4 (
    .in0(in_13), .in1(in_14), .in2(in_15), .in3(in_16), .out(multiplexer_4_out), .sel(Selection_Bit[1:0]));
  Multiplexer #(.select(2), .width(8), .disabled(0), .enable("false")) multiplexer_5 (
    .in0(multiplexer_1_out), .in1(multiplexer_2_out), .in2(multiplexer_3_out), .in3(multiplexer_4_out),
    .out(out_18), .sel(Selection_Bit[3:2]));

  // Notes on the sheet:
  //   Make a 16x1 multiplexor using any combo of 4x1 or 2x1 multiplexors
endmodule
