// Logisim project Assignment13_Circuits.circ as structural Verilog
module Black_Box_Mod4 (
  input  Q0,
  input  Q1,
  input  C,
  output Q0new,
  output Q1new
);

  wire and_1_out, and_2_out, and_3_out, and_4_out, and_5_out, not_1_out, not_2_out, not_3_out, not_4_out;

  not not_1 (not_1_out, Q0);
  not not_2 (not_2_out, C);
  not not_3 (not_3_out, Q1);
  not not_4 (not_4_out, not_2_out);
  and and_1 (and_1_out, Q0, not_4_out);
  and and_2 (and_2_out, not_1_out, not_2_out);
  and and_3 (and_3_out, Q0, not_3_out);
  and and_4 (and_4_out, Q0, not_4_out);
  and and_5 (and_5_out, not_1_out, Q1, not_2_out);
  or or_1 (Q0new, and_1_out, and_2_out);
  or or_2 (Q1new, and_3_out, and_4_out, and_5_out);

  // Notes on the sheet:
  //   BLACK BOX NEEDED FOR IMPLEMENTING PROBLEM 1 CIRCUIT
endmodule

module Problem1_Circuit (
  output Q0,
  output Q1
);

  wire black_box_mod4_1_q0new, black_box_mod4_1_q1new, clock_1_out;

  Clock clock_1 (.out(clock_1_out));
  Black_Box_Mod4 black_box_mod4_1 (
    .Q0(Q0), .Q1(Q1), .C(clock_1_out), .Q0new(black_box_mod4_1_q0new), .Q1new(black_box_mod4_1_q1new));
  D_Flip_Flop u_Q0 (.clk(clock_1_out), .D(black_box_mod4_1_q0new), .Q(Q0));  // open: Qn, preset, en, reset
  D_Flip_Flop u_Q1 (.clk(clock_1_out), .D(black_box_mod4_1_q1new), .Q(Q1));  // open: Qn, preset, en, reset

  // Notes on the sheet:
  //   Mod4 Black box
  //   Mod 4 Counter with problem 1 state diagram
endmodule

module Black_Box_Mod6 (
  input  Q0,
  input  Q1,
  input  Q2,
  output Q0_New,
  output Q1_New,
  output Q2_New
);

  ROM #(.addrWidth(3), .dataWidth(3)) rom_1 (.addr({Q2, Q1, Q0}), .data({Q2_New, Q1_New, Q0_New}));  // open: sel

  // Notes on the sheet:
  //   black box using 3 register input needed for problem 2 circuit implementation
  //   contents of rom_1 (hex, n*v repeats v):
  //   1 2 3 4 5
endmodule

module Problem2_Circuit (
  output Q0,
  output Q1,
  output Q2
);

  wire black_box_mod6_1_q0_new, black_box_mod6_1_q1_new, black_box_mod6_1_q2_new, undriven;

  Black_Box_Mod6 black_box_mod6_1 (
    .Q0(Q0), .Q1(Q1), .Q2(Q2), .Q0_New(black_box_mod6_1_q0_new), .Q1_New(black_box_mod6_1_q1_new),
    .Q2_New(black_box_mod6_1_q2_new));
  D_Flip_Flop u_Q0 (.clk(undriven), .D(black_box_mod6_1_q0_new), .Q(Q0));  // open: Qn, preset, en, reset
  D_Flip_Flop u_Q1 (.clk(undriven), .D(black_box_mod6_1_q1_new), .Q(Q1));  // open: Qn, preset, en, reset
  D_Flip_Flop u_Q2 (.clk(undriven), .D(black_box_mod6_1_q2_new), .Q(Q2));  // open: Qn, preset, en, reset

  // Notes on the sheet:
  //   Mod 6 counter using 3 registers and a 6x3 ROM
endmodule
